# Fritzing sketch Fritzing_Diagram_Automatic_Car_Gate_System_Gr2 (saved by Fritzing 1.0.2b)
breadboards: 1

parts:
  ZS-042_RTC2 = ZS-042 RTC Module
  J3 = Basic Servo
  hc-sr3 = HC-SR04 Ultrasonic Distance Sensor
  S2 = Pushbutton [package="[THT]"]
  microSD2 = MicroSD Card Module
  esp1 = ESP32 DevKitc V4

nets:
  GND: ZS-042_RTC2.GND, J3.gnd, hc-sr3.GND, S2.Pin_3, S2.Pin_4, microSD2.GND, esp1.CMD
  VCC: ZS-042_RTC2.VCC, J3.vcc, hc-sr3.VCC, microSD2.VCC, esp1.5V
  N1: ZS-042_RTC2.SDA, esp1.IO21
  N2: ZS-042_RTC2.SCL, esp1.IO22
  N3: J3.pulse, esp1.IO26
  N4: hc-sr3.TRIG, esp1.IO5
  N5: hc-sr3.ECHO, esp1.IO25
  N6: S2.Pin_1, S2.Pin_2, esp1.IO4
  N7: microSD2.MISO, esp1.IO19
  N8: microSD2.MOSI, esp1.IO23
  N9: microSD2.SCK, esp1.IO18
  N10: microSD2.CS, esp1.IO13

notes:
  Pin
  GPIO26 --> Servo Signal
  GPIO5 --> Ultrasonic TRIG
  GPIO25 --> Ultrasonic ECHO
  GPIO4 --> Switch Button
  GPIO13 --> SD_CS
  GPIO21 --> RTC_SDA
  GPIO22 --> RTC_SCL
  GPIO23 --> SD_MOSI
  GPIO19 --> SD_MISO
  GPIO18 --> SD_SCK

custom parts:
  ESP32 DevKitc V4: ESP32-DevKitC board with ESP32-WROOM-32 module. ESP32-DevKitC V4 is a small-sized ESP32-based development board produced by Espressif. Most of the pins on the ESP module are broken out to the pin headers on the board. The pins D0, D1, D2, D3, CMD and CLK are used internally for communication between ESP32 and SPI flash memory. They are grouped on both sides near the USB connector. Avoid using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
